// Logisim project cmsclogism.circ as structural Verilog: 1 circuit, main circuit main
module main (
  input  A,
  input  B,
  input  C,
  input  A2,
  input  B2,
  input  C2,
  input  A3,
  input  B3,
  input  C3,
  input  A4,
  input  B4,
  input  C4,
  input  A5,
  input  B5,
  input  C5,
  input  in_16,
  input  in_17,
  input  in_18,
  input  in_19,
  input  in_20,
  input  in_21,
  input  in_22,
  input  in_23,
  input  in_24,
  input  in_25,
  input  in_26,
  input  in_27,
  input  in_28,
  input  in_29,
  input  in_30,
  output ANDOR_F,
  output NAND_F
);

  wire and_1_out, and_2_out, and_3_out, and_4_out, and_6_out, and_7_out, and_9_out, and_11_out, and_12_out,
       and_13_out, and_14_out, not_1_out, not_2_out, not_3_out, not_4_out, not_5_out, not_6_out, not_7_out,
       not_8_out, not_9_out, not_10_out, not_11_out, not_12_out;

  not not_1 (not_1_out, A2);
  not not_2 (not_2_out, B4);
  not not_3 (not_3_out, in_19);
  not not_4 (not_4_out, in_26);
  not not_5 (not_5_out, B3);
  not not_6 (not_6_out, C3);
  not not_7 (not_7_out, A5);
  not not_8 (not_8_out, B5);
  not not_9 (not_9_out, in_23);
  not not_10 (not_10_out, in_24);
  not not_11 (not_11_out, in_28);
  not not_12 (not_12_out, in_29);
  and and_1 (and_1_out, A, C);
  and and_2 (and_2_out, not_1_out, C2);
  and and_3 (and_3_out, A3, not_6_out);
  and and_4 (and_4_out, A4, C4);
  and and_5 (and_4_out, not_7_out, C5);
  and and_6 (and_6_out, in_16, in_18);
  and and_7 (and_7_out, not_3_out, in_21);
  and and_8 (and_7_out, in_22, not_10_out);
  and and_9 (and_9_out, in_25, in_27);
  and and_10 (and_9_out, not_11_out, in_30);
  and and_11 (and_11_out, and_1_out, and_2_out);
  and and_12 (and_12_out, and_3_out, and_4_out);
  and and_13 (and_13_out, and_6_out, and_7_out);
  buf and_14 (and_14_out, and_9_out);  // AND_Gate
  or or_1 (ANDOR_F, and_11_out, and_12_out);
  and and_15 (NAND_F, and_13_out, and_14_out);
endmodule
